# Fritzing sketch electrical-schema (saved by Fritzing 0.9.0b)
breadboards: 1

parts:
  part = Arduino Uno (Rev3)
  R5 = Resistor [tolerance=±5% resistance=220 package=THT]
  LED5 = LED - 5mm [color="Red (633nm)" package="5 mm [THT]"]
  R6 = Rotary Potentiometer (Small) [maximum_resistance=10kΩ package=THT]

nets:
  N1: part.A0, R6.wiper
  N2: part.D13/SCK, R5.Pin_0
  N3: part.GND, LED5.cathode, R6.leg1
  N4: part.5V, R6.leg2
  N5: R5.Pin_1, LED5.anode
