# Fritzing sketch electrical-schema (saved by Fritzing 0.9.0b)
breadboards: 1

parts:
  Componente1 = Arduino Uno (Rev3)
  R3 = Resistor [tolerance=±5% resistance=220 package=THT]
  R4 = Resistor [tolerance=±5% resistance=220 package=THT]
  R5 = Resistor [tolerance=±5% resistance=220 package=THT]
  LED3 = LED - 5mm [color="Green (555nm)" package="5 mm [THT]"]
  LED4 = LED - 5mm [color="Yellow (574nm)" package="5 mm [THT]"]
  LED5 = LED - 5mm [color="Red (633nm)" package="5 mm [THT]"]

nets:
  N1: Componente1.D8, R3.Pin_0
  N2: Componente1.D9_PWM, R4.Pin_0
  N3: Componente1.D10_PWM/SS, R5.Pin_0
  N4: Componente1.GND, LED3.cathode, LED4.cathode, LED5.cathode
  N5: R3.Pin_1, LED3.anode
  N6: R4.Pin_1, LED4.anode
  N7: R5.Pin_1, LED5.anode
