# Fritzing sketch electrical-schema (saved by Fritzing 0.9.0b)
breadboards: 1

parts:
  Componente1 = Arduino Uno (Rev3)
  9g = Basic Servo
  part = Resistor [tolerance=±5% resistance=220 package=THT]
  2x = Resistor [tolerance=±5% resistance=220 package=THT]
  Stop = SWITCH-MOMENTARY-2 [package=tactile_switch_smd-2]
  Start = SWITCH-MOMENTARY-2 [package=tactile_switch_smd-2]

nets:
  N1: Componente1.D9_PWM, 9g.pulse
  N2: Componente1.D2, 2x.Pin_1, Start.1
  N3: Componente1.D3_PWM, part.Pin_1, Stop.1
  GND: 9g.gnd, part.Pin_0, 2x.Pin_0
  5V: 9g.vcc, Stop.2, Start.2
