# Fritzing sketch electrical-schema (saved by Fritzing 0.9.0b)
breadboards: 1

parts:
  Componente1 = Arduino Uno (Rev3)
  part = Resistor [tolerance=±5% resistance=220 package=THT]
  LED_RGB = RGB LED (com. cathode, rgb) [package="5 mm [THT]"]

nets:
  N1: Componente1.D9_PWM, LED_RGB.red_anode
  N2: Componente1.D10_PWM/SS, LED_RGB.blue_anode
  N3: Componente1.D11_PWM/MOSI, LED_RGB.green_anode
  GND: Componente1.GND, part.Pin_1
  N4: part.Pin_0, LED_RGB.common_cathode
