# Fritzing sketch electrical-schema (saved by Fritzing 0.9.0b)
breadboards: 1

parts:
  Componente1 = Arduino Uno (Rev3)
  R1 = Resistor [tolerance=±5% resistance=220 package=THT]
  R2 = Resistor [tolerance=±5% resistance=220 package=THT]
  R3 = Resistor [tolerance=±5% resistance=220 package=THT]
  R4 = Resistor [tolerance=±5% resistance=220 package=THT]
  R5 = Resistor [tolerance=±5% resistance=220 package=THT]
  R6 = Resistor [tolerance=±5% resistance=220 package=THT]
  part = LED - 5mm [color="Red (633nm)" package="5 mm [THT]"]
  part_2 = LED - 5mm [color="Green (555nm)" package="5 mm [THT]"]
  LED3 = LED - 5mm [color="Green (555nm)" package="5 mm [THT]"]
  LED4 = LED - 5mm [color="Yellow (574nm)" package="5 mm [THT]"]
  LED5 = LED - 5mm [color="Red (633nm)" package="5 mm [THT]"]
  S1 = Pushbutton [package="[THT]"]

nets:
  N1: Componente1.D8, R3.Pin_0
  N2: Componente1.D9_PWM, R4.Pin_0
  N3: Componente1.D10_PWM/SS, R5.Pin_0
  N4: Componente1.GND, R6.Pin_1, part.cathode, part_2.cathode, LED3.cathode, LED4.cathode, LED5.cathode
  N5: Componente1.D2, R6.Pin_0, S1.Pin_1, S1.Pin_2
  N6: Componente1.D5_PWM, R1.Pin_0
  N7: Componente1.D7, R2.Pin_0
  N8: Componente1.5V, S1.Pin_3, S1.Pin_4
  N9: R1.Pin_1, part_2.anode
  N10: R2.Pin_1, part.anode
  N11: R3.Pin_1, LED3.anode
  N12: R4.Pin_1, LED4.anode
  N13: R5.Pin_1, LED5.anode
