# Fritzing sketch electrical-schema (saved by Fritzing 0.9.0b)
breadboards: 1

parts:
  Componente1 = Arduino Uno (Rev3)
  R5 = Resistor [tolerance=±5% resistance=220 package=THT]
  LED5 = LED - 5mm [color="Red (633nm)" package="5 mm [THT]"]
  S1 = Pushbutton [package="[THT]"]
  R6 = Resistor [tolerance=±5% resistance=220 package=THT]

nets:
  N1: Componente1.D8, R5.Pin_0
  N2: Componente1.GND, LED5.cathode, R6.Pin_0
  N3: Componente1.D2, S1.Pin_1, S1.Pin_2, R6.Pin_1
  N4: Componente1.5V, S1.Pin_3, S1.Pin_4
  N5: R5.Pin_1, LED5.anode
