# Fritzing sketch RoboticArm (saved by Fritzing 0.9.4)
circuit board: 8.46667cm x 5.64444cm

parts:
  part = Arduino Uno (Rev3) - ICSP
  x-axis_control = POT [package=pot_alpha_rv16af-20]
  y-axis_control = POT [package=pot_alpha_rv16af-20]
  z-axis_control = POT [package=pot_alpha_rv16af-20]
  claw_control = POT [package=pot_alpha_rv16af-20]
  x-axis = Basic Servo
  y-axis = Basic Servo
  z-axis = Basic Servo
  claw = Basic Servo

nets:
  N1: part.A0, x-axis_control.S
  N2: part.A1, y-axis_control.S
  N3: part.A2, z-axis_control.S
  N4: part.A3, claw_control.S
  5V: part.5V, x-axis_control.E, y-axis_control.E, z-axis_control.E, claw_control.E, x-axis.vcc, y-axis.vcc, z-axis.vcc, claw.vcc
  GND: part.GND, x-axis_control.A, y-axis_control.A, z-axis_control.A, claw_control.A, x-axis.gnd, y-axis.gnd, z-axis.gnd, claw.gnd
  N5: part.D8, z-axis.pulse
  N6: part.D9_PWM, claw.pulse
  N7: part.D6_PWM, x-axis.pulse
  N8: part.D7, y-axis.pulse
