# Fritzing sketch electrical-schema (saved by Fritzing 0.9.0b)
breadboards: 1

parts:
  Componente1 = Arduino Uno (Rev3)
  9g = Basic Servo
  10k = POT [package=pot_alpha_rv16af-20]

nets:
  N1: Componente1.A0, 10k.S
  N2: Componente1.D9_PWM, 9g.pulse
  5V: Componente1.5V, 9g.vcc, 10k.E
  GND: Componente1.GND, 9g.gnd, 10k.A
