# Fritzing sketch electrical-schema (saved by Fritzing 0.9.0b)
breadboards: 1

parts:
  Componente1 = Arduino Uno (Rev3)
  J1 = Piezo Speaker
  part = Resistor [tolerance=±5% resistance=1k package=THT]
  part_2 = Resistor [tolerance=±5% resistance=220 package=THT]
  LED1 = LED - 5mm [color="Red (633nm)" package="5 mm [THT]"]

nets:
  N1: Componente1.D13/SCK, part_2.Pin_0
  N2: Componente1.GND, J1.pin2, part.Pin_0, LED1.cathode
  N3: Componente1.D3_PWM, J1.pin1, part.Pin_1
  N4: part_2.Pin_1, LED1.anode
