# Fritzing sketch electrical-schema (saved by Fritzing 0.9.0b)
breadboards: 1

parts:
  Componente1 = Arduino Uno (Rev3)
  Componente2 = ENC28J60 Breakout Board
  T1 = LM35 Temperature Sensor [package="TO92 [THT]"]
  part = Resistor [tolerance=±5% resistance=10k package=THT]

nets:
  N1: Componente1.A0, T1.Vout
  N2: Componente1.D8, Componente2.CS
  N3: Componente1.D11_PWM/MOSI, Componente2.SI
  N4: Componente1.D12/MISO, Componente2.SO
  N5: Componente1.D13/SCK, Componente2.SCK
  GND: Componente1.GND, Componente2.GND, T1.GND, part.Pin_0
  3.3V: Componente1.3V3, Componente2.VCC
  5V: T1.+Vs

custom parts:
  ENC28J60 Breakout Board: This is a breakout board for the Microchip ENC28J60 stand-alone ethernet controller. The ENC28J60 has an SPI interface. It operates at 3.3 Volts.
